# Fritzing sketch washing-machine (saved by Fritzing 0.9.3b)
circuit board: 6.88566cm x 5.36311cm
breadboards: 2

parts:
  VCC1 = Battery
  IC1 = ILD213T [package=so08]  # not connected
  attiny = attiny85 [package=dip]
  LED1 = LED - 3mm [color="Blue (430nm)" package="3 mm [THT]"]
  R1 = Resistor [tolerance=±5% resistance=330 package="0603 [SMD]"]
  S1 = Pushbutton [package="[THT]"]
  S2 = Pushbutton [package="[THT]"]
  R2 = Resistor [tolerance=±5% resistance=10 package="0603 [SMD]"]  # not connected
  R3 = Resistor [tolerance=±5% resistance=220 package="0603 [SMD]"]  # not connected

nets:
  N1: VCC1.-, attiny.Pin_4, LED1.cathode
  N2: VCC1.+, attiny.Pin_8, S1.Pin_1, S1.Pin_2, S2.Pin_1, S2.Pin_2
  N3: attiny.Pin_5, R1.Pin_1
  N4: attiny.Pin_6, S2.Pin_3, S2.Pin_4
  N5: attiny.Pin_7, S1.Pin_3, S1.Pin_4
  N6: LED1.anode, R1.Pin_0

notes:
  An optocoupler can be used to control a circuit that's completely isolated from your microcontroller in order to avoid the risk of short-circuit. In this case, imagine that the LED + battery pack combo is a hacked toy that you're turning on and off with the Arduino.
